// Logisim project DMF.circ as structural Verilog: 1 circuit, main circuit main
module main (
  input  q1,
  input  q0,
  input  BTN0_prime,
  input  BTN1_prime,
  output q0_prime,
  output q1_prime
);

  wire and_1_out, and_2_out, and_3_out, and_4_out, and_5_out, and_6_out;

  and and_1 (and_1_out, ~q0, BTN0_prime, ~BTN1_prime);  // AND_Gate
  and and_2 (and_2_out, q0, ~q1, BTN0_prime, BTN1_prime);  // AND_Gate
  and and_3 (and_3_out, q0, ~q1, ~BTN0_prime, ~BTN1_prime);  // AND_Gate
  and and_4 (and_4_out, ~q1, BTN1_prime, ~BTN0_prime);  // AND_Gate
  and and_5 (and_5_out, ~q0, q1, BTN0_prime, BTN1_prime);  // AND_Gate
  and and_6 (and_6_out, ~q0, q1, ~BTN0_prime, ~BTN1_prime);  // AND_Gate
  or or_1 (q0_prime, and_1_out, and_2_out, and_3_out);
  or or_2 (q1_prime, and_4_out, and_5_out, and_6_out);
endmodule
