// Logisim project FPGA.circ as structural Verilog: 6 circuits, main circuit FPGA_G3-G4
module FPGA_G3_G4 (
  input  CLK,
  input  CLK_2,
  output G4,
  output G3,
  output G4_2,
  output G3_2
);

  wire not_2_out;

  nor nor_1 (G4, not_2_out, CLK);
  and and_1 (G3, not_2_out, CLK);
  nor nor_2 (G4_2, 1'b0, 1'b1);
  and and_2 (G3_2, 1'b0, 1'b1);
  // NOT_Gate not_1 has open pins: in=1'b1, out=open
  not not_2 (not_2_out, CLK);

  // Notes on the sheet:
  //   Das zweite Schaltbild dient der Simulation der Verzögerung der Inverter. Hierzu können die Konstanten unabhängig voneinander mit 0x0 und 0x1 verwendet werden.
endmodule

module FPGA_G1_G2 (
  input  BTN2,
  input  BTN2_2,
  output G2,
  output G1,
  output BTN2_2NEG,
  output BTN2_NEG,
  output G2_2,
  output G1_2,
  output BTN2_2NEG_2,
  output BTN2_NEG_2
);

  nor nor_1 (G2, BTN2_2NEG, BTN2_NEG);
  and and_1 (G1, BTN2_NEG, BTN2_2NEG);
  nor nor_2 (G2_2, 1'b0, 1'b0);
  and and_2 (G1_2, 1'b0, 1'b0);
  not not_1 (BTN2_2NEG, BTN2_NEG);
  // NOT_Gate not_2 has open pins: in=1'b0, out=open
  not not_3 (BTN2_NEG, BTN2);
  // NOT_Gate not_4 has open pins: in=BTN2_2, out=open

  assign BTN2_2NEG_2 = 1'b0;
  assign BTN2_NEG_2 = 1'b0;

  // Notes on the sheet:
  //   Das zweite Schaltbild dient der Simulation der Verzögerung der Inverter. Hierzu können die Konstanten unabhängig voneinander mit 0x0 und 0x1 verwendet werden.
endmodule

module FPGA_RS2 (
  input  R,
  input  S,
  output Q,
  output Q_neg
);

  nand nand_1 (Q, R, Q_neg);
  nand nand_2 (Q_neg, Q, S);
endmodule

module FPGA_RS1 (
  input  R,
  input  S,
  output Q,
  output Q_neg
);

  nor nor_1 (Q, R, Q_neg);
  nor nor_2 (Q_neg, Q, S);
endmodule

module FPGA_G5_G8 (
  input  BTN0_Set,
  input  BTN1_Reset,
  input  BTN2_CLK,
  output Q2,
  output Q2_neg
);

  wire nand_3_out, nand_4_out;

  nand nand_1 (Q2, nand_3_out, Q2_neg);
  nand nand_2 (Q2_neg, nand_4_out, Q2);
  nand nand_3 (nand_3_out, BTN0_Set, BTN2_CLK);
  nand nand_4 (nand_4_out, BTN1_Reset, BTN2_CLK);
endmodule

module FPGA_G9_G12 (
  input  BTN0_Set,
  input  BTN1_Reset,
  input  BTN2_CLK,
  output Q2,
  output Q2_neg
);

  wire and_1_out, and_2_out;

  nor nor_1 (Q2, and_1_out, Q2_neg);
  nor nor_2 (Q2_neg, and_2_out, Q2);
  and and_1 (and_1_out, BTN1_Reset, BTN2_CLK);
  and and_2 (and_2_out, BTN0_Set, BTN2_CLK);
endmodule
