// Logisim project aufgabe_1d.circ as structural Verilog: 2 circuits, main circuit main
module main (
  input  BTN0,
  input  BTN1,
  input  CLK,
  output Q,
  output nQ,
  output Q_2,
  output nQ_2
);

  wire and_1_out, and_2_out, nand_3_out, nand_4_out;

  nor nor_1 (Q_2, and_1_out, nQ_2);
  nor nor_2 (nQ_2, Q_2, and_2_out);
  nand nand_1 (Q, nand_3_out, nQ);
  nand nand_2 (nQ, Q, nand_4_out);
  and and_1 (and_1_out, BTN1, CLK);
  and and_2 (and_2_out, CLK, BTN0);
  nand nand_3 (nand_3_out, CLK, BTN0);
  nand nand_4 (nand_4_out, CLK, BTN1);
endmodule

module main_andereGates (
  input  BTN0,
  input  BTN1,
  input  CLK,
  output Q,
  output nQ,
  output Q_2,
  output nQ_2
);

  wire and_1_out, and_2_out, and_3_out, and_4_out;

  nor nor_1 (Q_2, and_1_out, nQ_2);
  nor nor_2 (nQ_2, Q_2, and_2_out);
  nand nand_1 (Q, and_3_out, nQ);
  nand nand_2 (nQ, Q, and_4_out);
  and and_1 (and_1_out, BTN1, CLK);
  and and_2 (and_2_out, CLK, BTN0);
  and and_3 (and_3_out, CLK, BTN0);
  and and_4 (and_4_out, CLK, BTN1);

  // Notes on the sheet:
  //   getaktetes Active High RS Latch
  //   getaktetes Active Low RS Latch, kann mit NAND Gates zu einem getakteten Active High RS Latch gewandelt werden (siehe main)
endmodule
