// Logisim project schaltwerk.circ as structural Verilog: 1 circuit, main circuit main
module main (
  input  q1,
  input  q0,
  output q0_prime,
  output q1_prime
);

  wire and_1_out, and_2_out, and_3_out, and_4_out, and_5_out, and_6_out, and_7_out, and_8_out,
       BTN0_prime_out, BTN1_prime_out, clock_1_out, d_ff_1_q, d_ff_1_qn, d_ff_2_q, d_ff_2_qn, not_1_out,
       not_2_out, or_1_out, or_2_out;

  Button BTN0_prime (.out(BTN0_prime_out));
  Button BTN1_prime (.out(BTN1_prime_out));
  not not_1 (not_1_out, BTN0_prime_out);
  not not_2 (not_2_out, BTN1_prime_out);
  D_Flip_Flop d_ff_1 (.clk(and_1_out), .D(d_ff_1_qn), .Q(d_ff_1_q), .Qn(d_ff_1_qn));  // open: preset, en, reset
  and and_1 (and_1_out, BTN0_prime_out, not_1_out);
  D_Flip_Flop d_ff_2 (.clk(and_2_out), .D(d_ff_2_qn), .Q(d_ff_2_q), .Qn(d_ff_2_qn));  // open: preset, en, reset
  and and_2 (and_2_out, not_2_out, BTN1_prime_out);
  Clock clock_1 (.out(clock_1_out));
  and and_3 (and_3_out, ~q0, d_ff_1_q, ~d_ff_2_q);  // AND_Gate
  and and_4 (and_4_out, q0, ~q1, d_ff_1_q, d_ff_2_q);  // AND_Gate
  and and_5 (and_5_out, q0, ~q1, ~d_ff_1_q, ~d_ff_2_q);  // AND_Gate
  and and_6 (and_6_out, ~q1, d_ff_2_q, ~d_ff_1_q);  // AND_Gate
  and and_7 (and_7_out, ~q0, q1, d_ff_1_q, d_ff_2_q);  // AND_Gate
  and and_8 (and_8_out, ~q0, q1, ~d_ff_1_q, ~d_ff_2_q);  // AND_Gate
  or or_1 (or_1_out, and_3_out, and_4_out, and_5_out);
  or or_2 (or_2_out, and_6_out, and_7_out, and_8_out);
  D_Flip_Flop d_ff_3 (.clk(clock_1_out), .D(or_1_out), .Q(q0_prime));  // open: Qn, preset, en, reset
  D_Flip_Flop d_ff_4 (.clk(clock_1_out), .D(or_2_out), .Q(q1_prime));  // open: Qn, preset, en, reset
endmodule
